// Logisim project Central-Potating-Unit.circ as structural Verilog
module cpu (
);

  wire undriven;

  \reg  reg_1 ();  // open: in_1, out_3, in_2
  \reg  reg_2 (.in_1(undriven));  // open: out_3, in_2
  \reg  reg_3 (.in_1(undriven));  // open: out_3, in_2
  \reg  reg_4 (.in_1(undriven));  // open: out_3, in_2
  \reg  reg_5 (.in_1(undriven));  // open: out_3, in_2
  \reg  reg_6 (.in_1(undriven));  // open: out_3, in_2
  \reg  reg_7 (.in_1(undriven));  // open: out_3, in_2
  \reg  reg_8 (.in_1(undriven));  // open: out_3, in_2
  \reg  reg_9 (.in_1(undriven));  // open: out_3, in_2
endmodule

module \reg  (
  input  in_1,
  input  in_2,
  output out_3
);

  dlatch dlatch_1 (.in_1(in_1), .in_2(in_2), .out_3(out_3));  // open: out_4
endmodule

module dlatch (
  input  in_1,
  input  in_2,
  output out_3,
  output out_4
);

  wire and_1_out, and_2_out, not_1_out;

  not not_1 (not_1_out, in_1);
  and and_1 (and_1_out, not_1_out, in_2);
  rslatch rslatch_1 (.in_1(and_1_out), .in_2(and_2_out), .out_3(out_3), .out_4(out_4));
  and and_2 (and_2_out, in_1, in_2);
endmodule

module rslatch (
  input  in_1,
  input  in_2,
  output out_3,
  output out_4
);

  nor nor_1 (out_3, in_1, out_4);
  nor nor_2 (out_4, out_3, in_2);
endmodule
