// Logisim project Central-Potating-Unit.circ as structural Verilog
module cpu (
);

  wire undriven;

  \reg  reg_1 ();  // open: in_1, out_3, in_2
  \reg  reg_2 (.in_1(undriven));  // open: out_3, in_2
  \reg  reg_3 (.in_1(undriven));  // open: out_3, in_2
  \reg  reg_4 (.in_1(undriven));  // open: out_3, in_2
  \reg  reg_5 (.in_1(undriven));  // open: out_3, in_2
  \reg  reg_6 (.in_1(undriven));  // open: out_3, in_2
  \reg  reg_7 (.in_1(undriven));  // open: out_3, in_2
  \reg  reg_8 (.in_1(undriven));  // open: out_3, in_2
  \reg  reg_9 (.in_1(undriven));  // open: out_3, in_2
endmodule

module alu (
  input  [15:0] in_1,
  input  [15:0] in_2,
  input  [1:0] in_3,
  output out_4,
  output [15:0] out_5
);


  assign out_4 = 1'b0;
  assign out_5 = in_2;
endmodule

module \reg  (
  input  in_1,
  input  in_2,
  output out_3
);

  dlatch dlatch_1 (.in_1(in_1), .in_2(in_2), .out_3(out_3));  // open: out_4
endmodule

module dlatch (
  input  in_1,
  input  in_2,
  output out_3,
  output out_4
);

  wire and_1_out, and_2_out, not_1_out;

  not not_1 (not_1_out, in_1);
  and and_1 (and_1_out, not_1_out, in_2);
  rslatch rslatch_1 (.in_1(and_1_out), .in_2(and_2_out), .out_3(out_3), .out_4(out_4));
  and and_2 (and_2_out, in_1, in_2);
endmodule

module rslatch (
  input  in_1,
  input  in_2,
  output out_3,
  output out_4
);

  nor nor_1 (out_3, in_1, out_4);
  nor nor_2 (out_4, out_3, in_2);
endmodule

module mux10to1 (
  input  in_1,
  input  in_2,
  input  in_3,
  input  in_4,
  input  in_5,
  input  in_6,
  input  in_7,
  input  in_8,
  input  in_9,
  input  in_10,
  input  [3:0] in_11,
  output out_12
);


  assign out_12 = in_1;
endmodule

module cu (
  input  [8:0] in_1,
  input  in_2,
  input  in_3,
  input  in_4,
  output [3:0] out_5,
  output [1:0] out_6,
  output out_7
);


  assign out_5 = 4'b0000;
  assign out_6 = 2'b00;
  assign out_7 = in_3;
endmodule
